// Digital circuit DMA.dig as structural Verilog
module DMA (
  input  Q5,
  input  Q4,
  input  Q3,
  input  Q2,
  input  PHI2,
  input  SYNC,
  input  Q1,
  input  Q0,
  input  Q7,
  input  Q6,
  input  DS0,
  input  DS0_2,
  output S0A,
  output S1A,
  output nRW,
  output BE,
  output S0D,
  output S1D,
  output RDY,
  output nMR,
  output nIRQ,
  output nRES,
  output nOEA,
  output nOED
);

  wire and_1_out, and_2_out, and_3_out, d_ff_as_1_nq, d_ff_as_2_nq, d_ff_as_3_q, d_ff_as_4_q, nand_1_out,
       nand_2_out, nor_1_out, nor_3_out, nor_4_out, nor_5_out, nor_6_out, not_1_out, not_2_out, not_3_out,
       or_1_out, or_2_out;

  nand nand_1 (nand_1_out, and_1_out, Q1);
  nand nand_2 (nand_2_out, and_1_out, Q0);
  not not_1 (not_1_out, PHI2);
  nand nand_3 (nMR, Q7, not_1_out);
  and and_1 (and_1_out, PHI2, Q7);
  and and_2 (and_2_out, not_1_out, Q6);
  and and_3 (and_3_out, Q6, PHI2);
  D_FF_AS d_ff_as_1 (.Set(~1'b1), .D(1'b1), .C(SYNC), .Clr(~nand_1_out), .nQ(d_ff_as_1_nq));  // open: Q
  D_FF_AS d_ff_as_2 (.Set(~nand_1_out), .D(1'b0), .C(1'b0), .Clr(~nand_2_out), .nQ(d_ff_as_2_nq));  // open: Q
  nor nor_1 (nor_1_out, d_ff_as_2_nq, d_ff_as_1_nq);
  D_FF_AS d_ff_as_3 (.Set(~1'b1), .D(DS0_2), .C(nMR), .Clr(~1'b1), .Q(d_ff_as_3_q));  // open: nQ
  D_FF_AS d_ff_as_4 (.Set(~1'b1), .D(DS0), .C(nMR), .Clr(~1'b1), .Q(d_ff_as_4_q));  // open: nQ
  nor nor_2 (nOEA, and_2_out, and_1_out);
  or or_1 (or_1_out, and_3_out, nor_1_out);
  PullUp pullup_1 (.out(nRES));
  NFET nfet_1 (.G(d_ff_as_3_q), .D(nRES), .S(1'b0));
  PullUp pullup_2 (.out(nIRQ));
  NFET nfet_2 (.G(d_ff_as_4_q), .D(nIRQ), .S(1'b0));
  PullUp pullup_3 (.out(RDY));
  NFET nfet_3 (.G(or_1_out), .D(RDY), .S(1'b0));
  nor nor_3 (nor_3_out, Q5, Q4);
  nor nor_4 (nor_4_out, Q3, Q2);
  nor nor_5 (nor_5_out, S0A, nor_4_out);
  not not_2 (not_2_out, nOEA);
  not not_3 (not_3_out, nor_5_out);
  or or_2 (or_2_out, nor_5_out, BE);
  nor nor_6 (nor_6_out, not_3_out, BE);
  nand nand_4 (BE, not_2_out, nor_3_out);
  nor nor_7 (S0A, nOEA, nor_3_out);
  nor nor_8 (S0D, nOEA, nor_5_out);
  or or_3 (S1D, not_3_out, nOEA);
  PFET pfet_1 (.G(or_2_out), .S(1'b1), .D(nRW));
  NFET nfet_4 (.G(nor_6_out), .D(nRW), .S(1'b0));

  assign nOED = nOEA;
  assign S1A = BE;

  // Notes on the sheet:
  //   Q1: STEP
  //   Q0: RUN
  //   ADDR0 SR
  //   ADDR1 SR
  //   6502
  //   EXEC SR
  //   ~3
  //   2
  //   1
  //   0
  //   ~12
  //   RP6502 DMA
  //   by Rumbledethumps
  //   Instruction Set
  //   100000xx Read RAM
  //   100010xx Write RAM
  //   101000xx Read 6502
  //   1xxxxx10 Halt/Step 6502
  //   1xxxxx01 Run 6502
  //   ADDR SR
  //   DATA SR
  //   ALL SR
endmodule
