// Digital circuit RIA.dig as structural Verilog
module RIA (
  input  [15:0] ADDR,
  input  RWB,
  input  PHI2,
  input  IRQB_2,
  input  IRQB_3,
  output WE,
  output IRQB,
  output RIA,
  output VIA,
  output RAM
);

  wire IORQ, IORQB, nand_3_out, nand_4_out, nand_5_out, not_1_out, RREQ;

  nand nand_1 (IORQB, ADDR[8], ADDR[9], ADDR[10], ADDR[11], ADDR[12], ADDR[13], ADDR[14], ADDR[15]);
  nand nand_2 (WE, PHI2, not_1_out);
  not not_1 (not_1_out, RWB);
  nand nand_3 (nand_3_out, IRQB_2, IRQB_3);
  nand nand_4 (nand_4_out, ADDR[5], ADDR[6]);
  nand nand_5 (nand_5_out, ADDR[7], IORQ);
  not not_2 (IRQB, nand_3_out);
  nor nor_1 (RREQ, nand_4_out, nand_5_out);
  not not_3 (IORQ, IORQB);
  LookUpTable Pi_Pico (.in0(RREQ), .in1(1'b0), .out(RIA));
  LookUpTable _6522 (.in0(IORQ), .in1(RREQ), .out(VIA));
  LookUpTable SRAM (.in0(1'b0), .in1(IORQB), .out(RAM));

  // Other names for the same wires on the sheet: A0 = ADDR[0]; A1 = ADDR[1]; A2 = ADDR[2]; A3 = ADDR[3]; A4 = ADDR[4];
  //   A5 = ADDR[5]; A6 = ADDR[6]; A7 = ADDR[7]; A8 = ADDR[8]; A9 = ADDR[9]; A10 = ADDR[10]; A11 = ADDR[11];
  //   A12 = ADDR[12]; A13 = ADDR[13]; A14 = ADDR[14]; A15 = ADDR[15]

  // Notes on the sheet:
  //   ADDR: default 65024
  //   RWB: default 1
  //   PHI2: default 1
  //   IRQB_2: default 1
  //   IRQB_3: default 1
  //   7430
  //   CS
  //   N/C
  //   CS1
  //   CS2B
  //   CE#
  //   CE2
  //   contents of Pi_Pico (hex, n*v repeats v):
  //   0,1,0,1
  //   contents of _6522 (hex, n*v repeats v):
  //   0,1
  //   contents of SRAM (hex, n*v repeats v):
  //   0,a,1
endmodule

/* Test case:
ADDR   RIA VIA RAM
0x0000 0   0   1
0xfeff 0   0   1
0xff00 0   1   0
0xffdf 0   1   0
0xffe0 1   0   0
0xffff 1   0   0
*/
